# Fritzing sketch blue_pill_arduino_usb_hid_keyboard (saved by Fritzing 1.0.1rc)
breadboards: 1

parts:
  M1 = STM32F103C8T6 blue mini board
  Key6 = Pushbutton [package="[THT]"]
  Key5 = Pushbutton [package="[THT]"]
  Key4 = Pushbutton [package="[THT]"]
  Key3 = Pushbutton [package="[THT]"]
  Key2 = Pushbutton [package="[THT]"]
  Key1 = Pushbutton [package="[THT]"]
  Key0 = Pushbutton [package="[THT]"]

nets:
  N1: M1.G, M1.GND, Key6.Pin_3, Key6.Pin_4, Key5.Pin_3, Key5.Pin_4, Key4.Pin_3, Key4.Pin_4, Key3.Pin_3, Key3.Pin_4, Key2.Pin_3, Key2.Pin_4, Key1.Pin_3, Key1.Pin_4, Key0.Pin_3, Key0.Pin_4
  N2: M1.C13, Key6.Pin_1, Key6.Pin_2
  N3: M1.C14, Key5.Pin_1, Key5.Pin_2
  N4: M1.C15, Key4.Pin_1, Key4.Pin_2
  N5: M1.A0, Key3.Pin_1, Key3.Pin_2
  N6: M1.A1, Key2.Pin_1, Key2.Pin_2
  N7: M1.A2, Key1.Pin_1, Key1.Pin_2
  N8: M1.A3, Key0.Pin_1, Key0.Pin_2
